# Fritzing sketch zoetrope01 (saved by Fritzing 0.9.9b)
circuit board: 11.4965cm x 3.61078cm
breadboards: 1

parts:
  R2_-_Speed = Rotary Potentiometer (Large) [maximum_resistance=10kΩ part_number=Speed package=THT]
  Stepper_A = Screw terminal - 2 pins [part_number="Stepper A" package=THT]
  Stepper_Driver = Pololu A4988 [package=SO16]
  Power = Power plug [part_number=Power]
  Arduino_Nano = Arduino Nano (Rev3.0)
  Led_OUT = LED - 5mm [color="Red (633nm)" current=0.030 part_number=Flash package="5 mm [THT]"]
  R1_-_Flash = Rotary Potentiometer (Large) [maximum_resistance=10kΩ part_number=Intensity package=THT]
  R3_-_Frames = Rotary Potentiometer (Large) [maximum_resistance=10kΩ part_number=Frames package=THT]
  Q1 = Basic FET N-Channel [package="TO220 [THT]"]
  R4 = Resistor [tolerance=±5% power=0.25 resistance=220 package=THT]
  R5 = Resistor [tolerance=±5% power=0.25 resistance=100k package=THT]
  Stepper_B = screw terminal, 2 pins

nets (from the schematic view):
  GND: R2_-_Speed.leg1, Stepper_Driver.GND, Power.GND, Arduino_Nano.GND, R1_-_Flash.leg1, R3_-_Frames.leg1, Q1.source, R5.Pin_0
  N1: R2_-_Speed.wiper, Arduino_Nano.A1
  5v: R2_-_Speed.leg2, Stepper_Driver.VDD, R1_-_Flash.leg2, R3_-_Frames.leg2
  N2: Stepper_A.pin1, Stepper_Driver.1A
  N3: Stepper_A.pin2, Stepper_Driver.1B
  N4: Stepper_Driver.ENABLE, Arduino_Nano.D4
  N5: Stepper_Driver.RESET, Stepper_Driver.SLEEP
  N6: Stepper_Driver.STEP, Arduino_Nano.D2
  N7: Stepper_Driver.DIR, Arduino_Nano.D3
  N8: Stepper_Driver.2A, Stepper_B.pin2
  N9: Stepper_Driver.2B, Stepper_B.pin1
  12V: Stepper_Driver.VMOT, Power.VCC, Arduino_Nano.VIN, Led_OUT.anode
  N10: Arduino_Nano.D5, R4.Pin_0
  N11: Arduino_Nano.A2, R3_-_Frames.wiper
  N12: Arduino_Nano.A0, R1_-_Flash.wiper
  N13: Led_OUT.cathode, Q1.drain
  N14: Q1.gate, R4.Pin_1, R5.Pin_1
